// Logisim project questao1 - Gabriel Monteiro de Souza.circ as structural Verilog: 1 circuit, main circuit main
module main (
  input  A,
  input  B,
  input  C,
  input  D,
  input  E,
  output out_6
);

  wire A_B__prime_C_out, A_B__prime_D__prime_E_out, A_B__prime_D__prime_out, A_B__prime_out, C_prime_out,
       D_prime_out, nand_1_out;

  not C_prime (C_prime_out, C);
  not D_prime (D_prime_out, D);
  nand A_B__prime (A_B__prime_out, A, B);
  or A_B__prime_C (A_B__prime_C_out, A_B__prime_out, C);
  nor A_B__prime_D__prime (A_B__prime_D__prime_out, A_B__prime_out, D);
  or A_B__prime_D__prime_E (A_B__prime_D__prime_E_out, A_B__prime_D__prime_out, E);
  nand nand_1 (nand_1_out, A_B__prime_C_out, A_B__prime_D__prime_E_out, C_prime_out, D_prime_out);
  or u_E (out_6, nand_1_out, E);
endmodule
