// Logisim project questao2 - Gabriel Monteiro de Souza.circ as structural Verilog: 1 circuit, main circuit main
module main (
  input  _0,
  input  _1,
  input  _2,
  input  _3,
  input  _4,
  input  _5,
  input  _6,
  input  A,
  input  B,
  input  C,
  input  _7,
  output X,
  output Y,
  output Z
);

  wire and_1_out, and_2_out, and_3_out, and_4_out, and_5_out, and_6_out, and_7_out, and_8_out, and_9_out,
       and_10_out, and_11_out, and_12_out, decoder_1_out0, decoder_1_out1, decoder_1_out2, decoder_1_out3,
       decoder_1_out4, decoder_1_out5, decoder_1_out6, decoder_1_out7, not_1_out, not_2_out, not_3_out;

  Priority_Encoder priority_encoder_1 (
    .in0(_0), .in1(_1), .in2(_2), .in3(_3), .in4(_4), .in5(_5), .in6(_6), .in7(_7), .out({A, B, C}));  // open: en_in, gs, en_out
  not not_1 (not_1_out, A);
  not not_2 (not_2_out, B);
  not not_3 (not_3_out, C);
  LED u__0 (.in(decoder_1_out0));
  LED u__1 (.in(decoder_1_out1));
  LED u__2 (.in(decoder_1_out2));
  LED u__3 (.in(decoder_1_out3));
  LED u__4 (.in(decoder_1_out4));
  LED u__5 (.in(decoder_1_out5));
  LED u__6 (.in(decoder_1_out6));
  Decoder #(.select(3), .enable("false")) decoder_1 (
    .out0(decoder_1_out0), .out1(decoder_1_out1), .out2(decoder_1_out2), .out3(decoder_1_out3),
    .out4(decoder_1_out4), .out5(decoder_1_out5), .out6(decoder_1_out6), .out7(decoder_1_out7),
    .sel({X, Y, Z}));
  LED u__7 (.in(decoder_1_out7));
  and and_1 (and_1_out, A, not_2_out, not_3_out);
  and and_2 (and_2_out, A, B, not_3_out);
  and and_3 (and_3_out, A, not_2_out, C);
  and and_4 (and_4_out, A, B, C);
  and and_5 (and_5_out, A, not_2_out, not_3_out);
  and and_6 (and_6_out, not_1_out, B, not_3_out);
  and and_7 (and_7_out, A, not_2_out, C);
  and and_8 (and_8_out, not_1_out, B, C);
  and and_9 (and_9_out, not_1_out, B, not_3_out);
  and and_10 (and_10_out, A, B, not_3_out);
  and and_11 (and_11_out, not_1_out, not_2_out, C);
  and and_12 (and_12_out, A, not_2_out, C);
  or or_1 (X, and_1_out, and_2_out, and_3_out, and_4_out);
  or or_2 (Y, and_5_out, and_6_out, and_7_out, and_8_out);
  or or_3 (Z, and_9_out, and_10_out, and_11_out, and_12_out);
endmodule
