// Logisim project revisaoP1.circ as structural Verilog: 1 circuit, main circuit main
module main (
  input  Vem,
  input  X,
  input  Y,
  input  in_4,
  input  in_5,
  output S,
  output Vai
);

  wire and_1_out, and_2_out, nor_1_out, nor_2_out, xor_1_out;

  nor nor_1 (nor_1_out, in_4, nor_2_out);
  nor nor_2 (nor_2_out, nor_1_out, in_5);
  xor xor_1 (xor_1_out, X, Y);
  and and_1 (and_1_out, X, Y);
  xor xor_2 (S, Vem, xor_1_out);
  and and_2 (and_2_out, Vem, xor_1_out);
  or or_1 (Vai, and_2_out, and_1_out);
endmodule
